// Logisim project CRC.circ as structural Verilog: 2 circuits, main circuit CRC
module CRC (
  input  [7:0] in_1,
  input  [3:0] in_2,
  output [10:0] out_3
);

  wire _0, _1, _2, _3, _4, _5, _6;
  wire [2:0] div_1_out_3, div_2_out_3, div_3_out_3, div_4_out_3, div_5_out_3, div_6_out_3, div_7_out_3;
  wire [3:0] _710;
  wire [10:0] bit_extender_1_out;

  assign bit_extender_1_out = {{3{1'b0}}, in_1};  // Bit_Extender bit_extender_1
  Shifter #(.width(11)) shifter_1 (.in(bit_extender_1_out), .\dist (4'b0011), .out({_710, _6, _5, _4, _3, _2, _1, _0}));
  div div_1 (.in_1(_710), .in_2(in_2), .out_3(div_1_out_3));
  div div_2 (.in_1({div_1_out_3, _6}), .in_2(in_2), .out_3(div_2_out_3));
  div div_3 (.in_1({div_2_out_3, _5}), .in_2(in_2), .out_3(div_3_out_3));
  div div_4 (.in_1({div_3_out_3, _4}), .in_2(in_2), .out_3(div_4_out_3));
  div div_5 (.in_1({div_4_out_3, _3}), .in_2(in_2), .out_3(div_5_out_3));
  div div_6 (.in_1({div_5_out_3, _2}), .in_2(in_2), .out_3(div_6_out_3));
  div div_7 (.in_1({div_6_out_3, _1}), .in_2(in_2), .out_3(div_7_out_3));
  div div_8 (.in_1({div_7_out_3, _0}), .in_2(in_2), .out_3(out_3[2:0]));

  assign out_3[10:3] = in_1;

  // Other names for the same wires on the sheet: d[3:0] = in_2; in[7:0] = in_1
endmodule

module div (
  input  [3:0] in_1,
  input  [3:0] in_2,
  output [2:0] out_3
);

  wire not_1_out;
  wire [3:0] multiplexer_1_out, xor_1_out;

  assign xor_1_out = in_1 ^ in_2;  // XOR_Gate xor_1, 4 bits wide
  Bit_Extender #(.in_width(4), .out_width(3)) bit_extender_1 (.in(multiplexer_1_out), .out(out_3));
  Multiplexer #(.width(4)) multiplexer_1 (
    .in0(xor_1_out), .in1(in_1), .out(multiplexer_1_out), .sel(not_1_out));  // open: en
  not not_1 (not_1_out, in_1[3]);
endmodule
