// Logisim project GRF - 副本 (2).circ as structural Verilog: 1 circuit, main circuit grf
module grf (
  input  clk,
  input  reset,
  input  WE,
  input  [31:0] WD,
  input  [4:0] A1,
  input  [4:0] A2,
  input  [4:0] A3,
  output [31:0] RD1,
  output [31:0] RD2
);

  wire [31:0] i0, i1, i2, i3, i4, i5, i6, i7, i8, i9, i10, i11, i12, i13, i14, i15, i16, i17, i18, i19, i20,
       i21, i22, i23, i24, i25, i26, i27, i28, i29, i30, i31, multiplexer_3_out, multiplexer_4_out, o0, o1,
       o2, o3, o4, o5, o6, o7, o8, o9, o10, o11, o12, o13, o14, o15, o16, o17, o18, o19, o20, o21, o22, o23,
       o24, o25, o26, o27, o28, o29, o30, o31;

  Multiplexer #(.select(5), .width(32)) multiplexer_1 (
    .in0(o0), .in1(o1), .in2(o2), .in3(o3), .in4(o4), .in5(o5), .in6(o6), .in7(o7), .in8(o8), .in9(o9),
    .in10(o10), .in11(o11), .in12(o12), .in13(o13), .in14(o14), .in15(o15), .in16(o16), .in17(o17),
    .in18(o18), .in19(o19), .in20(o20), .in21(o21), .in22(o22), .in23(o23), .in24(o24), .in25(o25),
    .in26(o26), .in27(o27), .in28(o28), .in29(o29), .in30(o30), .in31(o31), .out(RD1), .sel(A1));  // open: en
  Register #(.width(32)) register_1 (.D({32{1'b0}}), .Q(o0), .clk(clk), .clr(reset));  // open: en
  Register #(.width(32)) register_2 (.D(i8), .Q(o8), .clk(clk), .clr(reset));  // open: en
  Register #(.width(32)) register_3 (.D(i16), .Q(o16), .clk(clk), .clr(reset));  // open: en
  Register #(.width(32)) register_4 (.D(i24), .Q(o24), .clk(clk), .clr(reset));  // open: en
  Register #(.width(32)) register_5 (.D(i1), .Q(o1), .clk(clk), .clr(reset));  // open: en
  Register #(.width(32)) register_6 (.D(i9), .Q(o9), .clk(clk), .clr(reset));  // open: en
  Register #(.width(32)) register_7 (.D(i17), .Q(o17), .clk(clk), .clr(reset));  // open: en
  Register #(.width(32)) register_8 (.D(i25), .Q(o25), .clk(clk), .clr(reset));  // open: en
  Multiplexer #(.select(5), .width(32)) multiplexer_2 (
    .in0(o0), .in1(o1), .in2(o2), .in3(o3), .in4(o4), .in5(o5), .in6(o6), .in7(o7), .in8(o8), .in9(o9),
    .in10(o10), .in11(o11), .in12(o12), .in13(o13), .in14(o14), .in15(o15), .in16(o16), .in17(o17),
    .in18(o18), .in19(o19), .in20(o20), .in21(o21), .in22(o22), .in23(o23), .in24(o24), .in25(o25),
    .in26(o26), .in27(o27), .in28(o28), .in29(o29), .in30(o30), .in31(o31), .out(RD2), .sel(A2));  // open: en
  Register #(.width(32)) register_9 (.D(i2), .Q(o2), .clk(clk), .clr(reset));  // open: en
  Register #(.width(32)) register_10 (.D(i10), .Q(o10), .clk(clk), .clr(reset));  // open: en
  Register #(.width(32)) register_11 (.D(i18), .Q(o18), .clk(clk), .clr(reset));  // open: en
  Register #(.width(32)) register_12 (.D(i26), .Q(o26), .clk(clk), .clr(reset));  // open: en
  Register #(.width(32)) register_13 (.D(i3), .Q(o3), .clk(clk), .clr(reset));  // open: en
  Register #(.width(32)) register_14 (.D(i11), .Q(o11), .clk(clk), .clr(reset));  // open: en
  Register #(.width(32)) register_15 (.D(i19), .Q(o19), .clk(clk), .clr(reset));  // open: en
  Register #(.width(32)) register_16 (.D(i27), .Q(o27), .clk(clk), .clr(reset));  // open: en
  Register #(.width(32)) register_17 (.D(i4), .Q(o4), .clk(clk), .clr(reset));  // open: en
  Register #(.width(32)) register_18 (.D(i12), .Q(o12), .clk(clk), .clr(reset));  // open: en
  Register #(.width(32)) register_19 (.D(i20), .Q(o20), .clk(clk), .clr(reset));  // open: en
  Register #(.width(32)) register_20 (.D(i28), .Q(o28), .clk(clk), .clr(reset));  // open: en
  Multiplexer #(.select(5), .width(32)) multiplexer_3 (
    .in0(o0), .in1(o1), .in2(o2), .in3(o3), .in4(o4), .in5(o5), .in6(o6), .in7(o7), .in8(o8), .in9(o9),
    .in10(o10), .in11(o11), .in12(o12), .in13(o13), .in14(o14), .in15(o15), .in16(o16), .in17(o17),
    .in18(o18), .in19(o19), .in20(o20), .in21(o21), .in22(o22), .in23(o23), .in24(o24), .in25(o25),
    .in26(o26), .in27(o27), .in28(o28), .in29(o29), .in30(o30), .in31(o31), .out(multiplexer_3_out), .sel(A3));  // open: en
  Register #(.width(32)) register_21 (.D(i5), .Q(o5), .clk(clk), .clr(reset));  // open: en
  Register #(.width(32)) register_22 (.D(i13), .Q(o13), .clk(clk), .clr(reset));  // open: en
  Register #(.width(32)) register_23 (.D(i21), .Q(o21), .clk(clk), .clr(reset));  // open: en
  Register #(.width(32)) register_24 (.D(i29), .Q(o29), .clk(clk), .clr(reset));  // open: en
  Multiplexer #(.width(32)) multiplexer_4 (
    .in0(multiplexer_3_out), .in1(WD), .out(multiplexer_4_out), .sel(WE));  // open: en
  Demultiplexer #(.select(5), .width(32), .tristate("true")) demultiplexer_1 (
    .out0(i0), .out1(i1), .out2(i2), .out3(i3), .out4(i4), .out5(i5), .out6(i6), .out7(i7), .out8(i8),
    .out9(i9), .out10(i10), .out11(i11), .out12(i12), .out13(i13), .out14(i14), .out15(i15), .out16(i16),
    .out17(i17), .out18(i18), .out19(i19), .out20(i20), .out21(i21), .out22(i22), .out23(i23), .out24(i24),
    .out25(i25), .out26(i26), .out27(i27), .out28(i28), .out29(i29), .out30(i30), .out31(i31),
    .in(multiplexer_4_out), .sel(A3));  // open: en
  Register #(.width(32)) register_25 (.D(i6), .Q(o6), .clk(clk), .clr(reset));  // open: en
  Register #(.width(32)) register_26 (.D(i14), .Q(o14), .clk(clk), .clr(reset));  // open: en
  Register #(.width(32)) register_27 (.D(i22), .Q(o22), .clk(clk), .clr(reset));  // open: en
  Register #(.width(32)) register_28 (.D(i30), .Q(o30), .clk(clk), .clr(reset));  // open: en
  Register #(.width(32)) register_29 (.D(i7), .Q(o7), .clk(clk), .clr(reset));  // open: en
  Register #(.width(32)) register_30 (.D(i15), .Q(o15), .clk(clk), .clr(reset));  // open: en
  Register #(.width(32)) register_31 (.D(i23), .Q(o23), .clk(clk), .clr(reset));  // open: en
  Register #(.width(32)) register_32 (.D(i31), .Q(o31), .clk(clk), .clr(reset));  // open: en

  // Other names for the same wires on the sheet: c = clk; rs = reset
endmodule
