// Logisim project GRF - 副本.circ as structural Verilog: 1 circuit, main circuit grf
module grf (
  input  reset,
  input  WE,
  input  [31:0] WD,
  input  clk,
  input  [4:0] A1,
  input  [4:0] A2,
  input  [4:0] A3,
  output [31:0] RD1,
  output [31:0] RD2
);

  wire and_1_out, c0, c1, c2, c3, c4, c5, c6, c7, c8, c9, c10, c11, c12, c13, c14, c15, c16, c17, c18, c19,
       c20, c21, c22, c23, c24, c25, c26, c27, c28, c29, c30, c31;
  wire [31:0] o0, o1, o2, o3, o4, o5, o6, o7, o8, o9, o10, o11, o12, o13, o14, o15, o16, o17, o18, o19, o20,
       o21, o22, o23, o24, o25, o26, o27, o28, o29, o30, o31;

  Multiplexer #(.select(5), .width(32)) multiplexer_1 (
    .in0(o0), .in1(o1), .in2(o2), .in3(o3), .in4(o4), .in5(o5), .in6(o6), .in7(o7), .in8(o8), .in9(o9),
    .in10(o10), .in11(o11), .in12(o12), .in13(o13), .in14(o14), .in15(o15), .in16(o16), .in17(o17),
    .in18(o18), .in19(o19), .in20(o20), .in21(o21), .in22(o22), .in23(o23), .in24(o24), .in25(o25),
    .in26(o26), .in27(o27), .in28(o28), .in29(o29), .in30(o30), .in31(o31), .out(RD1), .sel(A1));  // open: en
  Register #(.width(32)) register_1 (.D({32{1'b0}}), .Q(o0), .clk(c0), .clr(reset));  // open: en
  Register #(.width(32)) register_2 (.D(WD), .Q(o8), .clk(c8), .clr(reset));  // open: en
  Register #(.width(32)) register_3 (.D(WD), .Q(o16), .clk(c16), .clr(reset));  // open: en
  Register #(.width(32)) register_4 (.D(WD), .Q(o24), .clk(c24), .clr(reset));  // open: en
  Register #(.width(32)) register_5 (.D(WD), .Q(o1), .clk(c1), .clr(reset));  // open: en
  Register #(.width(32)) register_6 (.D(WD), .Q(o9), .clk(c9), .clr(reset));  // open: en
  Register #(.width(32)) register_7 (.D(WD), .Q(o17), .clk(c17), .clr(reset));  // open: en
  Register #(.width(32)) register_8 (.D(WD), .Q(o25), .clk(c25), .clr(reset));  // open: en
  Multiplexer #(.select(5), .width(32)) multiplexer_2 (
    .in0(o0), .in1(o1), .in2(o2), .in3(o3), .in4(o4), .in5(o5), .in6(o6), .in7(o7), .in8(o8), .in9(o9),
    .in10(o10), .in11(o11), .in12(o12), .in13(o13), .in14(o14), .in15(o15), .in16(o16), .in17(o17),
    .in18(o18), .in19(o19), .in20(o20), .in21(o21), .in22(o22), .in23(o23), .in24(o24), .in25(o25),
    .in26(o26), .in27(o27), .in28(o28), .in29(o29), .in30(o30), .in31(o31), .out(RD2), .sel(A2));  // open: en
  Register #(.width(32)) register_9 (.D(WD), .Q(o2), .clk(c2), .clr(reset));  // open: en
  Register #(.width(32)) register_10 (.D(WD), .Q(o10), .clk(c10), .clr(reset));  // open: en
  Register #(.width(32)) register_11 (.D(WD), .Q(o18), .clk(c18), .clr(reset));  // open: en
  Register #(.width(32)) register_12 (.D(WD), .Q(o26), .clk(c26), .clr(reset));  // open: en
  Register #(.width(32)) register_13 (.D(WD), .Q(o3), .clk(c3), .clr(reset));  // open: en
  Register #(.width(32)) register_14 (.D(WD), .Q(o11), .clk(c11), .clr(reset));  // open: en
  Register #(.width(32)) register_15 (.D(WD), .Q(o19), .clk(c19), .clr(reset));  // open: en
  Register #(.width(32)) register_16 (.D(WD), .Q(o27), .clk(c27), .clr(reset));  // open: en
  Register #(.width(32)) register_17 (.D(WD), .Q(o4), .clk(c4), .clr(reset));  // open: en
  Register #(.width(32)) register_18 (.D(WD), .Q(o12), .clk(c12), .clr(reset));  // open: en
  Register #(.width(32)) register_19 (.D(WD), .Q(o20), .clk(c20), .clr(reset));  // open: en
  Register #(.width(32)) register_20 (.D(WD), .Q(o28), .clk(c28), .clr(reset));  // open: en
  Register #(.width(32)) register_21 (.D(WD), .Q(o5), .clk(c5), .clr(reset));  // open: en
  Register #(.width(32)) register_22 (.D(WD), .Q(o13), .clk(c13), .clr(reset));  // open: en
  Register #(.width(32)) register_23 (.D(WD), .Q(o21), .clk(c21), .clr(reset));  // open: en
  Register #(.width(32)) register_24 (.D(WD), .Q(o29), .clk(c29), .clr(reset));  // open: en
  Register #(.width(32)) register_25 (.D(WD), .Q(o6), .clk(c6), .clr(reset));  // open: en
  Register #(.width(32)) register_26 (.D(WD), .Q(o14), .clk(c14), .clr(reset));  // open: en
  Register #(.width(32)) register_27 (.D(WD), .Q(o22), .clk(c22), .clr(reset));  // open: en
  Register #(.width(32)) register_28 (.D(WD), .Q(o30), .clk(c30), .clr(reset));  // open: en
  and and_1 (and_1_out, WE, clk);
  Demultiplexer #(.select(5)) demultiplexer_1 (
    .out0(c0), .out1(c1), .out2(c2), .out3(c3), .out4(c4), .out5(c5), .out6(c6), .out7(c7), .out8(c8),
    .out9(c9), .out10(c10), .out11(c11), .out12(c12), .out13(c13), .out14(c14), .out15(c15), .out16(c16),
    .out17(c17), .out18(c18), .out19(c19), .out20(c20), .out21(c21), .out22(c22), .out23(c23), .out24(c24),
    .out25(c25), .out26(c26), .out27(c27), .out28(c28), .out29(c29), .out30(c30), .out31(c31),
    .in(and_1_out), .sel(A3));  // open: en
  Register #(.width(32)) register_29 (.D(WD), .Q(o7), .clk(c7), .clr(reset));  // open: en
  Register #(.width(32)) register_30 (.D(WD), .Q(o15), .clk(c15), .clr(reset));  // open: en
  Register #(.width(32)) register_31 (.D(WD), .Q(o23), .clk(c23), .clr(reset));  // open: en
  Register #(.width(32)) register_32 (.D(WD), .Q(o31), .clk(c31), .clr(reset));  // open: en

  // Other names for the same wires on the sheet: i[31:0] = WD; rs = reset
endmodule
