// Logisim project fsm - 副本.circ as structural Verilog: 2 circuits, main circuit fsm
module fsm (
  input  [1:0] In,
  input  CLR,
  output Z
);

  wire clock_1_out;
  wire [2:0] fsm_1_c_2, multiplexer_1_out, register_1_q;

  fsm_2 fsm_1 (
    .a(register_1_q[2]), .b(register_1_q[1]), .c(register_1_q[0]), .d(In[1]), .e(In[0]), .A_2(fsm_1_c_2[2]),
    .B_2(fsm_1_c_2[1]), .C_2(fsm_1_c_2[0]));
  Multiplexer #(.width(3)) multiplexer_1 (
    .in0(fsm_1_c_2), .in1(3'b000), .out(multiplexer_1_out), .sel(CLR));  // open: en
  Register #(.width(3)) register_1 (.D(multiplexer_1_out), .Q(register_1_q), .clk(clock_1_out));  // open: en, clr
  Clock clock_1 (.out(clock_1_out));
  // Probe on fsm_1_c_2
  Comparator #(.width(3), .mode("unsigned")) comparator_1 (.a(register_1_q), .b(3'b100), .eq(Z));  // open: gt, lt
  // Probe on register_1_q
endmodule

module fsm_2 (
  input  a,
  input  b,
  input  c,
  input  d,
  input  e,
  output A_2,
  output B_2,
  output C_2
);

  wire and_2_out, and_3_out, and_4_out, and_5_out, and_6_out, and_7_out, and_8_out, and_9_out, not_1_out,
       not_2_out, not_3_out, not_4_out, not_5_out, not_6_out, not_7_out, not_8_out, not_9_out, not_10_out,
       not_11_out, not_12_out, not_13_out, not_14_out, not_15_out, not_16_out, not_17_out, not_18_out,
       not_19_out, not_20_out, not_21_out, not_22_out, not_23_out, not_24_out, not_25_out;

  not not_1 (not_1_out, a);
  not not_2 (not_2_out, e);
  not not_3 (not_3_out, a);
  not not_4 (not_4_out, b);
  not not_5 (not_5_out, d);
  not not_6 (not_6_out, a);
  not not_7 (not_7_out, b);
  not not_8 (not_8_out, e);
  not not_9 (not_9_out, a);
  not not_10 (not_10_out, c);
  not not_11 (not_11_out, d);
  not not_12 (not_12_out, a);
  not not_13 (not_13_out, c);
  not not_14 (not_14_out, e);
  not not_15 (not_15_out, b);
  not not_16 (not_16_out, c);
  not not_17 (not_17_out, d);
  not not_18 (not_18_out, a);
  not not_19 (not_19_out, b);
  not not_20 (not_20_out, e);
  not not_21 (not_21_out, a);
  not not_22 (not_22_out, c);
  not not_23 (not_23_out, e);
  not not_24 (not_24_out, a);
  not not_25 (not_25_out, d);
  and and_1 (A_2, not_1_out, b, c, not_2_out);
  and and_2 (and_2_out, not_3_out, not_4_out, c, not_5_out);
  and and_3 (and_3_out, not_6_out, not_7_out, c, not_8_out);
  and and_4 (and_4_out, not_9_out, b, not_10_out, not_11_out);
  and and_5 (and_5_out, not_12_out, b, not_13_out, not_14_out);
  and and_6 (and_6_out, not_15_out, not_16_out, not_17_out, e);
  and and_7 (and_7_out, not_18_out, not_19_out, c, not_20_out);
  and and_8 (and_8_out, not_21_out, b, not_22_out, not_23_out);
  and and_9 (and_9_out, not_24_out, b, c, not_25_out, e);
  or or_1 (B_2, and_2_out, and_3_out, and_4_out, and_5_out);
  or or_2 (C_2, and_6_out, and_7_out, and_8_out, and_9_out);
endmodule
