// Logisim project ftoi.circ as structural Verilog: 1 circuit, main circuit ftoi
module ftoi (
  input  [15:0] float,
  output [31:0] \int 
);

  wire comparator_1_gt, comparator_2_eq;
  wire [4:0] E, subtractor_2_out;
  wire [31:0] multiplexer_1_out, multiplexer_2_out, multiplexer_3_out, negator_1_out, shifter_1_out;

  Subtractor #(.width(5)) subtractor_1 (.a(float[14:10]), .b(5'b01111), .out(E));  // open: bin, bout
  Subtractor #(.width(5)) subtractor_2 (.a({5{1'b1}}), .b(E), .out(subtractor_2_out));  // open: bin, bout
  Shifter #(.width(32), .shift("lr")) shifter_1 (
    .in({1'b1, float[9:0], {21{1'b0}}}), .\dist (subtractor_2_out), .out(shifter_1_out));
  Negator #(.width(32)) negator_1 (.in(shifter_1_out), .out(negator_1_out));
  Multiplexer #(.width(32)) multiplexer_1 (
    .in0(shifter_1_out), .in1(negator_1_out), .out(multiplexer_1_out), .sel(float[15]));  // open: en
  Multiplexer #(.width(32)) multiplexer_2 (
    .in0(multiplexer_1_out), .in1({32{1'b0}}), .out(multiplexer_2_out), .sel(comparator_1_gt));  // open: en
  Comparator #(.width(5), .mode("unsigned")) comparator_1 (.a(E), .b({5{1'b1}}), .gt(comparator_1_gt));  // open: eq, lt
  Multiplexer #(.width(32)) multiplexer_3 (
    .in0(multiplexer_2_out), .in1({32{1'b0}}), .out(multiplexer_3_out), .sel(E[4]));  // open: en
  Multiplexer #(.width(32)) multiplexer_4 (
    .in0(multiplexer_3_out), .in1({32{1'b0}}), .out(\int ), .sel(comparator_2_eq));  // open: en
  Comparator #(.width(5), .mode("unsigned")) comparator_2 (
    .a(float[14:10]), .b({5{1'b1}}), .eq(comparator_2_eq));  // open: gt, lt

  // Other names for the same wires on the sheet: f[9:0] = float[9:0]; e_t[4:0] = float[14:10]; s = float[15]
endmodule
