// Logisim project navigation - 副本 (2).circ as structural Verilog: 2 circuits, main circuit navigation
module navigation (
  input  [1:0] dir,
  input  clk,
  input  reset,
  output arrive,
  output hit
);

  wire clock_1_out;
  wire [4:0] register_1_q;
  wire [4:2] fsm_1_c_2;

  Clock clock_1 (.out(clock_1_out));
  fsm fsm_1 (
    .a(register_1_q[4]), .b(register_1_q[3]), .c(register_1_q[2]), .d(dir[1]), .e(dir[0]),
    .A_2(fsm_1_c_2[4]), .B_2(fsm_1_c_2[3]), .C_2(fsm_1_c_2[2]), .f(arrive), .g(hit));
  Register #(.width(5)) register_1 (
    .D({fsm_1_c_2, arrive, hit}), .Q(register_1_q), .clk(clock_1_out), .clr(reset));  // open: en
  // Probe on {fsm_1_c_2, arrive, hit}
  // Probe on register_1_q
endmodule

module fsm (
  input  a,
  input  b,
  input  c,
  input  d,
  input  e,
  output A_2,
  output B_2,
  output C_2,
  output f,
  output g
);

  wire and_1_out, and_2_out, and_3_out, and_4_out, and_5_out, and_6_out, and_7_out, and_8_out, and_9_out,
       and_10_out, and_11_out, and_12_out, and_13_out, and_14_out, and_15_out, and_16_out, and_17_out,
       and_18_out, not_1_out, not_2_out, not_3_out, not_4_out, not_5_out, not_6_out, not_7_out, not_8_out,
       not_9_out, not_10_out, not_11_out, not_12_out, not_13_out, not_14_out, not_15_out, not_16_out,
       not_17_out, not_18_out, not_19_out, not_20_out, not_21_out, not_22_out, not_23_out, not_24_out,
       not_25_out, not_26_out, not_27_out, not_28_out, not_29_out, not_30_out, not_31_out, not_32_out,
       not_33_out, not_34_out, not_35_out, not_36_out, not_37_out, not_38_out, not_39_out, not_40_out,
       not_41_out, not_42_out, not_43_out, not_44_out, not_45_out, not_46_out;

  not not_1 (not_1_out, a);
  not not_2 (not_2_out, c);
  not not_3 (not_3_out, d);
  not not_4 (not_4_out, e);
  not not_5 (not_5_out, a);
  not not_6 (not_6_out, d);
  not not_7 (not_7_out, a);
  not not_8 (not_8_out, b);
  not not_9 (not_9_out, d);
  not not_10 (not_10_out, a);
  not not_11 (not_11_out, d);
  not not_12 (not_12_out, e);
  not not_13 (not_13_out, a);
  not not_14 (not_14_out, c);
  not not_15 (not_15_out, d);
  not not_16 (not_16_out, a);
  not not_17 (not_17_out, c);
  not not_18 (not_18_out, e);
  not not_19 (not_19_out, a);
  not not_20 (not_20_out, a);
  not not_21 (not_21_out, b);
  not not_22 (not_22_out, d);
  not not_23 (not_23_out, e);
  not not_24 (not_24_out, a);
  not not_25 (not_25_out, a);
  not not_26 (not_26_out, a);
  not not_27 (not_27_out, e);
  not not_28 (not_28_out, a);
  not not_29 (not_29_out, c);
  not not_30 (not_30_out, d);
  not not_31 (not_31_out, e);
  not not_32 (not_32_out, a);
  not not_33 (not_33_out, d);
  not not_34 (not_34_out, a);
  not not_35 (not_35_out, c);
  not not_36 (not_36_out, d);
  not not_37 (not_37_out, a);
  not not_38 (not_38_out, b);
  not not_39 (not_39_out, c);
  not not_40 (not_40_out, a);
  not not_41 (not_41_out, c);
  not not_42 (not_42_out, e);
  not not_43 (not_43_out, a);
  not not_44 (not_44_out, a);
  not not_45 (not_45_out, d);
  not not_46 (not_46_out, e);
  and and_1 (and_1_out, not_1_out, b, not_2_out, not_3_out, not_4_out);
  and and_2 (and_2_out, not_5_out, b, c, not_6_out, e);
  and and_3 (and_3_out, not_7_out, not_8_out, c, not_9_out);
  and and_4 (and_4_out, not_10_out, c, not_11_out, not_12_out);
  and and_5 (and_5_out, not_13_out, b, not_14_out, not_15_out, e);
  and and_6 (and_6_out, not_16_out, b, not_17_out, d, not_18_out);
  and and_7 (and_7_out, not_19_out, b, c, d, e);
  and and_8 (and_8_out, not_20_out, not_21_out, not_22_out, not_23_out);
  and and_9 (and_9_out, not_24_out, c, d, e);
  and and_10 (and_10_out, not_25_out, b, d, e);
  and and_11 (and_11_out, not_26_out, b, c, not_27_out);
  and and_12 (and_12_out, not_28_out, b, not_29_out, not_30_out, not_31_out);
  and and_13 (and_13_out, not_32_out, b, c, not_33_out, e);
  and and_14 (and_14_out, not_34_out, not_35_out, not_36_out, e);
  and and_15 (and_15_out, not_37_out, not_38_out, not_39_out, d);
  and and_16 (and_16_out, not_40_out, not_41_out, d, not_42_out);
  and and_17 (and_17_out, not_43_out, c, d, e);
  and and_18 (and_18_out, not_44_out, b, c, not_45_out, not_46_out);
  or or_1 (A_2, and_1_out, and_2_out);
  or or_2 (B_2, and_3_out, and_4_out, and_5_out, and_6_out, and_7_out);
  or or_3 (C_2, and_8_out, and_9_out, and_10_out, and_11_out);
  or or_4 (f, and_12_out, and_13_out);
  or or_5 (g, and_14_out, and_15_out, and_16_out, and_17_out, and_18_out);
endmodule
