// Logisim project CPU有ALUCTL.circ as structural Verilog: 9 circuits, main circuit main
module main (
  input  in_1,
  output [31:0] out_2,
  output out_3,
  output [4:0] out_4,
  output [31:0] out_5,
  output out_6,
  output [4:0] out_7,
  output [31:0] out_8
);

  wire Branch, clk, MemRead, PCSrc, RegDst, Zero;
  wire [1:0] ALUOp, ALUSrc, MemtoReg;
  wire [2:0] ALU_op;
  wire [4:0] Rd, Rs, Rt;
  wire [5:0] Func, Op;
  wire [15:0] imm16;
  wire [31:0] adder_2_out, DMdata, lui, multiplexer_4_out, PC_4, PCin, PCout, Rd1, Ret, shifter_1_out, si32,
       usi32;

  Multiplexer #(.width(5), .enable("false")) multiplexer_1 (.in0(Rt), .in1(Rd), .out(out_4), .sel(RegDst));
  Shifter #(.width(32)) shifter_1 (.in(si32), .\dist (5'b00010), .out(shifter_1_out));
  Multiplexer #(.select(2), .width(32), .disabled(0), .enable("false")) multiplexer_2 (
    .in0({Ret[31:7], out_7, Ret[1:0]}), .in1(DMdata), .in2(lui), .out(out_5), .sel(MemtoReg));  // open: in3
  Adder #(.width(32)) adder_1 (.a(32'h4), .b(PCout), .out(PC_4));  // open: cin, cout
  Adder #(.width(32)) adder_2 (.a(PC_4), .b(shifter_1_out), .out(adder_2_out));  // open: cin, cout
  Controller controller_1 (
    .Op(Op), .out_5(Branch), .out_2(MemtoReg), .out_6(out_6), .out_7(MemRead), .out_3(ALUOp), .out_4(ALUSrc),
    .out_8(out_3), .out_9(RegDst));
  Multiplexer #(.width(32), .enable("false")) multiplexer_3 (.in0(PC_4), .in1(adder_2_out), .out(PCin), .sel(PCSrc));
  GRF grf_1 (.clk(clk), .reset(in_1), .WE(out_3), .WD(out_5), .A1(Rs), .A2(Rt), .A3(out_4), .RD1(Rd1), .RD2(out_8));
  IFU ifu_1 (.PCin(PCin), .Instr(out_2), .clk(clk), .reset(in_1), .PCout(PCout));
  Multiplexer #(.select(2), .width(32), .enable("false")) multiplexer_4 (
    .in0(out_8), .in1(usi32), .in2(si32), .out(multiplexer_4_out), .sel(ALUSrc));  // open: in3
  ALU_Controller alu_controller_1 (.Func(Func), .ALUOp(ALUOp), .ALU_op(ALU_op));
  ALU alu_1 (.A(Rd1), .B(multiplexer_4_out), .OP(ALU_op), .Result({Ret[31:7], out_7, Ret[1:0]}), .Zero(Zero));
  EXT ext_1 (.in_1(imm16), .out_2(usi32), .out_3(si32));
  Clock clock_1 (.out(clk));
  Splitter splitter_1 (.In(out_2), .Op(Op), .Rs(Rs), .Rt(Rt), .Rd(Rd), .Func(Func), .imm16(imm16));  // open: j
  Shifter #(.width(32)) shifter_2 (.in(usi32), .\dist (5'b10000), .out(lui));
  and and_1 (PCSrc, Zero, Branch);
  DM dm_1 (.in_1(out_7), .in_2(out_8), .out_7(DMdata), .in_3(out_6), .in_4(clk), .in_5(MemRead), .in_6(in_1));

  // Other names for the same wires on the sheet: Instr[31:0] = out_2; MemWrite = out_6; Rd2[31:0] = out_8;
  //   RegAddr[4:0] = out_4; RegData[31:0] = out_5; RegWrite = out_3; reset = in_1; MemAddr[4:0] = out_7;
  //   Ret[6:2] = out_7
endmodule

module ALU (
  input  [31:0] A,
  input  [31:0] B,
  input  [2:0] OP,
  output [31:0] Result,
  output Zero
);

  wire comparator_1_eq, comparator_2_eq;
  wire [31:0] ADD, AND, OR, SUB;

  assign AND = A & B;  // AND_Gate and_1, 32 bits wide
  assign OR = A | B;  // OR_Gate or_1, 32 bits wide
  Adder #(.width(32)) adder_1 (.a(A), .b(B), .out(ADD));  // open: cin, cout
  Subtractor #(.width(32)) subtractor_1 (.a(A), .b(B), .out(SUB));  // open: bin, bout
  Multiplexer #(.select(3), .width(32), .disabled(0)) multiplexer_1 (
    .in0(AND), .in1(OR), .in2(ADD), .in3(SUB), .out(Result), .sel(OP));  // open: in4, in5, in6, in7, en
  Comparator #(.width(32), .mode("unsigned")) comparator_1 (
    .a(SUB), .b({32{1'b0}}), .eq(comparator_1_eq));  // open: gt, lt
  Comparator #(.width(3), .mode("unsigned")) comparator_2 (.a(OP), .b(3'b100), .eq(comparator_2_eq));  // open: gt, lt
  and and_2 (Zero, comparator_1_eq, comparator_2_eq);
endmodule

module GRF (
  input  clk,
  input  reset,
  input  WE,
  input  [31:0] WD,
  input  [4:0] A1,
  input  [4:0] A2,
  input  [4:0] A3,
  output [31:0] RD1,
  output [31:0] RD2
);

  wire and_1_out, and_2_out, and_3_out, and_4_out, and_5_out, and_6_out, and_7_out, and_8_out, and_9_out,
       and_10_out, and_11_out, and_12_out, and_13_out, and_14_out, and_15_out, and_16_out, and_17_out,
       and_18_out, and_19_out, and_20_out, and_21_out, and_22_out, and_23_out, and_24_out, and_25_out,
       and_26_out, and_27_out, and_28_out, and_29_out, and_30_out, and_31_out, d0, d1, d2, d3, d4, d5, d6,
       d7, d8, d9, d10, d11, d12, d13, d14, d15, d16, d17, d18, d19, d20, d21, d22, d23, d24, d25, d26, d27,
       d28, d29, d30, d31;
  wire [31:0] i0, i1, i2, i3, i4, i5, i6, i7, i8, i9, i10, i11, i12, i13, i14, i15, i16, i17, i18, i19, i20,
       i21, i22, i23, i24, i25, i26, i27, i28, i29, i30, i31, o0, o1, o2, o3, o4, o5, o6, o7, o8, o9, o10,
       o11, o12, o13, o14, o15, o16, o17, o18, o19, o20, o21, o22, o23, o24, o25, o26, o27, o28, o29, o30,
       o31;

  Multiplexer #(.select(5), .width(32)) multiplexer_1 (
    .in0(o0), .in1(o1), .in2(o2), .in3(o3), .in4(o4), .in5(o5), .in6(o6), .in7(o7), .in8(o8), .in9(o9),
    .in10(o10), .in11(o11), .in12(o12), .in13(o13), .in14(o14), .in15(o15), .in16(o16), .in17(o17),
    .in18(o18), .in19(o19), .in20(o20), .in21(o21), .in22(o22), .in23(o23), .in24(o24), .in25(o25),
    .in26(o26), .in27(o27), .in28(o28), .in29(o29), .in30(o30), .in31(o31), .out(RD1), .sel(A1));  // open: en
  Register #(.width(32)) register_1 (.D(i0), .Q(o0), .clk(clk), .clr(reset));  // open: en
  Register #(.width(32)) register_2 (.D(i8), .Q(o8), .clk(clk), .clr(reset));  // open: en
  Register #(.width(32)) register_3 (.D(i16), .Q(o16), .clk(clk), .clr(reset));  // open: en
  Register #(.width(32)) register_4 (.D(i24), .Q(o24), .clk(clk), .clr(reset));  // open: en
  Register #(.width(32)) register_5 (.D(i1), .Q(o1), .clk(clk), .clr(reset));  // open: en
  Register #(.width(32)) register_6 (.D(i9), .Q(o9), .clk(clk), .clr(reset));  // open: en
  Register #(.width(32)) register_7 (.D(i17), .Q(o17), .clk(clk), .clr(reset));  // open: en
  Register #(.width(32)) register_8 (.D(i25), .Q(o25), .clk(clk), .clr(reset));  // open: en
  Multiplexer #(.select(5), .width(32)) multiplexer_2 (
    .in0(o0), .in1(o1), .in2(o2), .in3(o3), .in4(o4), .in5(o5), .in6(o6), .in7(o7), .in8(o8), .in9(o9),
    .in10(o10), .in11(o11), .in12(o12), .in13(o13), .in14(o14), .in15(o15), .in16(o16), .in17(o17),
    .in18(o18), .in19(o19), .in20(o20), .in21(o21), .in22(o22), .in23(o23), .in24(o24), .in25(o25),
    .in26(o26), .in27(o27), .in28(o28), .in29(o29), .in30(o30), .in31(o31), .out(RD2), .sel(A2));  // open: en
  Register #(.width(32)) register_9 (.D(i2), .Q(o2), .clk(clk), .clr(reset));  // open: en
  Register #(.width(32)) register_10 (.D(i10), .Q(o10), .clk(clk), .clr(reset));  // open: en
  Register #(.width(32)) register_11 (.D(i18), .Q(o18), .clk(clk), .clr(reset));  // open: en
  Register #(.width(32)) register_12 (.D(i26), .Q(o26), .clk(clk), .clr(reset));  // open: en
  Register #(.width(32)) register_13 (.D(i3), .Q(o3), .clk(clk), .clr(reset));  // open: en
  Register #(.width(32)) register_14 (.D(i11), .Q(o11), .clk(clk), .clr(reset));  // open: en
  Register #(.width(32)) register_15 (.D(i19), .Q(o19), .clk(clk), .clr(reset));  // open: en
  Register #(.width(32)) register_16 (.D(i27), .Q(o27), .clk(clk), .clr(reset));  // open: en
  Register #(.width(32)) register_17 (.D(i4), .Q(o4), .clk(clk), .clr(reset));  // open: en
  Register #(.width(32)) register_18 (.D(i12), .Q(o12), .clk(clk), .clr(reset));  // open: en
  Register #(.width(32)) register_19 (.D(i20), .Q(o20), .clk(clk), .clr(reset));  // open: en
  Register #(.width(32)) register_20 (.D(i28), .Q(o28), .clk(clk), .clr(reset));  // open: en
  Decoder #(.select(5)) decoder_1 (
    .out0(d0), .out1(d1), .out2(d2), .out3(d3), .out4(d4), .out5(d5), .out6(d6), .out7(d7), .out8(d8),
    .out9(d9), .out10(d10), .out11(d11), .out12(d12), .out13(d13), .out14(d14), .out15(d15), .out16(d16),
    .out17(d17), .out18(d18), .out19(d19), .out20(d20), .out21(d21), .out22(d22), .out23(d23), .out24(d24),
    .out25(d25), .out26(d26), .out27(d27), .out28(d28), .out29(d29), .out30(d30), .out31(d31), .sel(A3));  // open: en
  Register #(.width(32)) register_21 (.D(i5), .Q(o5), .clk(clk), .clr(reset));  // open: en
  Register #(.width(32)) register_22 (.D(i13), .Q(o13), .clk(clk), .clr(reset));  // open: en
  Register #(.width(32)) register_23 (.D(i21), .Q(o21), .clk(clk), .clr(reset));  // open: en
  Register #(.width(32)) register_24 (.D(i29), .Q(o29), .clk(clk), .clr(reset));  // open: en
  Register #(.width(32)) register_25 (.D(i6), .Q(o6), .clk(clk), .clr(reset));  // open: en
  Register #(.width(32)) register_26 (.D(i14), .Q(o14), .clk(clk), .clr(reset));  // open: en
  Register #(.width(32)) register_27 (.D(i22), .Q(o22), .clk(clk), .clr(reset));  // open: en
  Register #(.width(32)) register_28 (.D(i30), .Q(o30), .clk(clk), .clr(reset));  // open: en
  Multiplexer #(.width(32)) multiplexer_3 (.in0(o0), .in1(WD), .out(i0), .sel(1'b0));  // open: en
  Multiplexer #(.width(32)) multiplexer_4 (.in0(o4), .in1(WD), .out(i4), .sel(and_1_out));  // open: en
  and and_1 (and_1_out, d4, WE);
  Multiplexer #(.width(32)) multiplexer_5 (.in0(o8), .in1(WD), .out(i8), .sel(and_2_out));  // open: en
  and and_2 (and_2_out, d8, WE);
  Multiplexer #(.width(32)) multiplexer_6 (.in0(o12), .in1(WD), .out(i12), .sel(and_3_out));  // open: en
  buf and_3 (and_3_out, d12);  // AND_Gate
  Multiplexer #(.width(32)) multiplexer_7 (.in0(o16), .in1(WD), .out(i16), .sel(and_4_out));  // open: en
  and and_4 (and_4_out, d16, WE);
  Multiplexer #(.width(32)) multiplexer_8 (.in0(o20), .in1(WD), .out(i20), .sel(and_5_out));  // open: en
  buf and_5 (and_5_out, d20);  // AND_Gate
  Multiplexer #(.width(32)) multiplexer_9 (.in0(o24), .in1(WD), .out(i24), .sel(and_6_out));  // open: en
  and and_6 (and_6_out, d24, WE);
  Multiplexer #(.width(32)) multiplexer_10 (.in0(o28), .in1(WD), .out(i28), .sel(and_7_out));  // open: en
  buf and_7 (and_7_out, d28);  // AND_Gate
  Register #(.width(32)) register_29 (.D(i7), .Q(o7), .clk(clk), .clr(reset));  // open: en
  Register #(.width(32)) register_30 (.D(i15), .Q(o15), .clk(clk), .clr(reset));  // open: en
  Register #(.width(32)) register_31 (.D(i23), .Q(o23), .clk(clk), .clr(reset));  // open: en
  Register #(.width(32)) register_32 (.D(i31), .Q(o31), .clk(clk), .clr(reset));  // open: en
  Multiplexer #(.width(32)) multiplexer_11 (.in0(o1), .in1(WD), .out(i1), .sel(and_8_out));  // open: en
  and and_8 (and_8_out, d1, WE);
  Multiplexer #(.width(32)) multiplexer_12 (.in0(o5), .in1(WD), .out(i5), .sel(and_9_out));  // open: en
  and and_9 (and_9_out, d5, WE);
  Multiplexer #(.width(32)) multiplexer_13 (.in0(o9), .in1(WD), .out(i9), .sel(and_10_out));  // open: en
  and and_10 (and_10_out, d9, WE);
  Multiplexer #(.width(32)) multiplexer_14 (.in0(o13), .in1(WD), .out(i13), .sel(and_11_out));  // open: en
  buf and_11 (and_11_out, d13);  // AND_Gate
  Multiplexer #(.width(32)) multiplexer_15 (.in0(o17), .in1(WD), .out(i17), .sel(and_12_out));  // open: en
  and and_12 (and_12_out, d17, WE);
  Multiplexer #(.width(32)) multiplexer_16 (.in0(o21), .in1(WD), .out(i21), .sel(and_13_out));  // open: en
  buf and_13 (and_13_out, d21);  // AND_Gate
  Multiplexer #(.width(32)) multiplexer_17 (.in0(o25), .in1(WD), .out(i25), .sel(and_14_out));  // open: en
  and and_14 (and_14_out, d25, WE);
  Multiplexer #(.width(32)) multiplexer_18 (.in0(o29), .in1(WD), .out(i29), .sel(and_15_out));  // open: en
  buf and_15 (and_15_out, d29);  // AND_Gate
  Multiplexer #(.width(32)) multiplexer_19 (.in0(o2), .in1(WD), .out(i2), .sel(and_16_out));  // open: en
  and and_16 (and_16_out, d2, WE);
  Multiplexer #(.width(32)) multiplexer_20 (.in0(o6), .in1(WD), .out(i6), .sel(and_17_out));  // open: en
  and and_17 (and_17_out, d6, WE);
  Multiplexer #(.width(32)) multiplexer_21 (.in0(o10), .in1(WD), .out(i10), .sel(and_18_out));  // open: en
  and and_18 (and_18_out, d10, WE);
  Multiplexer #(.width(32)) multiplexer_22 (.in0(o14), .in1(WD), .out(i14), .sel(and_19_out));  // open: en
  buf and_19 (and_19_out, d14);  // AND_Gate
  Multiplexer #(.width(32)) multiplexer_23 (.in0(o18), .in1(WD), .out(i18), .sel(and_20_out));  // open: en
  and and_20 (and_20_out, d18, WE);
  Multiplexer #(.width(32)) multiplexer_24 (.in0(o22), .in1(WD), .out(i22), .sel(and_21_out));  // open: en
  buf and_21 (and_21_out, d22);  // AND_Gate
  Multiplexer #(.width(32)) multiplexer_25 (.in0(o26), .in1(WD), .out(i26), .sel(and_22_out));  // open: en
  and and_22 (and_22_out, d26, WE);
  Multiplexer #(.width(32)) multiplexer_26 (.in0(o30), .in1(WD), .out(i30), .sel(and_23_out));  // open: en
  buf and_23 (and_23_out, d30);  // AND_Gate
  Multiplexer #(.width(32)) multiplexer_27 (.in0(o3), .in1(WD), .out(i3), .sel(and_24_out));  // open: en
  and and_24 (and_24_out, d3, WE);
  Multiplexer #(.width(32)) multiplexer_28 (.in0(o7), .in1(WD), .out(i7), .sel(and_25_out));  // open: en
  and and_25 (and_25_out, d7, WE);
  Multiplexer #(.width(32)) multiplexer_29 (.in0(o11), .in1(WD), .out(i11), .sel(and_26_out));  // open: en
  and and_26 (and_26_out, d11, WE);
  Multiplexer #(.width(32)) multiplexer_30 (.in0(o15), .in1(WD), .out(i15), .sel(and_27_out));  // open: en
  buf and_27 (and_27_out, d15);  // AND_Gate
  Multiplexer #(.width(32)) multiplexer_31 (.in0(o19), .in1(WD), .out(i19), .sel(and_28_out));  // open: en
  and and_28 (and_28_out, d19, WE);
  Multiplexer #(.width(32)) multiplexer_32 (.in0(o23), .in1(WD), .out(i23), .sel(and_29_out));  // open: en
  buf and_29 (and_29_out, d23);  // AND_Gate
  Multiplexer #(.width(32)) multiplexer_33 (.in0(o27), .in1(WD), .out(i27), .sel(and_30_out));  // open: en
  and and_30 (and_30_out, d27, WE);
  Multiplexer #(.width(32)) multiplexer_34 (.in0(o31), .in1(WD), .out(i31), .sel(and_31_out));  // open: en
  buf and_31 (and_31_out, d31);  // AND_Gate

  // Other names for the same wires on the sheet: c = clk; rs = reset
endmodule

module Splitter (
  input  [31:0] In,
  output [5:0] Op,
  output [4:0] Rs,
  output [4:0] Rt,
  output [4:0] Rd,
  output [5:0] Func,
  output [15:0] imm16,
  output [25:0] j
);


  assign Func = In[5:0];
  assign imm16 = In[15:0];
  assign j = In[25:0];
  assign Op = In[31:26];
  assign Rd = In[15:11];
  assign Rs = In[25:21];
  assign Rt = In[20:16];
endmodule

module Controller (
  input  [5:0] Op,
  output [1:0] out_2,
  output [1:0] out_3,
  output [1:0] out_4,
  output out_5,
  output out_6,
  output out_7,
  output out_8,
  output out_9
);

  wire beq_out, lui_out, lw_out, not_1_out, not_2_out, not_3_out, not_4_out, not_5_out, not_6_out, ori_out,
       R_out, sw_out;

  not not_1 (not_1_out, Op[5]);
  not not_2 (not_2_out, Op[4]);
  not not_3 (not_3_out, Op[3]);
  not not_4 (not_4_out, Op[1]);
  not not_5 (not_5_out, Op[2]);
  not not_6 (not_6_out, Op[0]);
  and R (R_out, not_1_out, not_2_out, not_3_out, not_5_out, not_4_out, not_6_out);
  and ori (ori_out, not_1_out, not_2_out, Op[3], Op[2], not_4_out, Op[0]);
  and lw (lw_out, Op[5], not_2_out, not_3_out, not_5_out, Op[1], Op[0]);
  and sw (sw_out, Op[5], not_2_out, Op[3], not_5_out, Op[1], Op[0]);
  and beq (beq_out, not_1_out, not_2_out, not_3_out, Op[2], not_4_out, not_6_out);
  and lui (lui_out, not_1_out, not_2_out, Op[3], Op[2], Op[1], Op[0]);
  buf Branch (out_5, beq_out);  // OR_Gate
  buf MemtoReg_1 (out_2[1], lui_out);  // OR_Gate
  buf MemtoReg_0 (out_2[0], lw_out);  // OR_Gate
  buf MemWrite (out_6, sw_out);  // OR_Gate
  buf MemRead (out_7, lw_out);  // OR_Gate
  or ALUOp_0 (out_3[0], ori_out, beq_out);
  or ALUOp_1 (out_3[1], lw_out, sw_out, beq_out);
  or ALUSrc_1 (out_4[1], lw_out, sw_out);
  or ALUSrc_0 (out_4[0], ori_out, lui_out);
  buf RegDst (out_9, R_out);  // OR_Gate
  or RegWrite (out_8, R_out, ori_out, lw_out, lui_out);
endmodule

module ALU_Controller (
  input  [5:0] Func,
  input  [1:0] ALUOp,
  output [2:0] ALU_op
);

  wire addu_out, beq_out, lw_sw_out, not_1_out, not_2_out, not_3_out, not_4_out, not_5_out, not_6_out,
       not_7_out, not_8_out, ori_out, subu_out;

  not not_1 (not_1_out, Func[4]);
  not not_2 (not_2_out, Func[5]);
  not not_3 (not_3_out, Func[3]);
  not not_4 (not_4_out, Func[2]);
  not not_5 (not_5_out, Func[1]);
  not not_6 (not_6_out, Func[0]);
  not not_7 (not_7_out, ALUOp[1]);
  not not_8 (not_8_out, ALUOp[0]);
  buf _2 (ALU_op[2], beq_out);  // OR_Gate
  and addu (addu_out, Func[5], not_1_out, not_3_out, not_4_out, not_5_out, Func[0], not_7_out, not_8_out);
  and subu (subu_out, Func[5], not_1_out, not_3_out, not_4_out, Func[1], Func[0], not_7_out, not_8_out);
  and ori (ori_out, not_7_out, ALUOp[0]);
  and lw_sw (lw_sw_out, ALUOp[1], not_8_out);
  and beq (beq_out, ALUOp[1], ALUOp[0]);
  or _1 (ALU_op[1], addu_out, subu_out, lw_sw_out);
  or _0 (ALU_op[0], subu_out, ori_out);
endmodule

module IFU (
  input  [31:0] PCin,
  input  clk,
  input  reset,
  output [31:0] PCout,
  output [31:0] Instr
);

  Register #(.width(32)) register_1 (.D(PCin), .Q(PCout), .clk(clk), .clr(reset));  // open: en
  ROM #(.addrWidth(5), .dataWidth(32)) rom_1 (.addr(PCout[6:2]), .data(Instr));  // open: sel
endmodule

module DM (
  input  [4:0] in_1,
  input  [31:0] in_2,
  input  in_3,
  input  in_4,
  input  in_5,
  input  in_6,
  output [31:0] out_7
);

  RAM #(.addrWidth(5), .dataWidth(32), .bus("separate")) ram_1 (
    .addr(in_1), .din(in_2), .data(out_7), .str(in_3), .clk(in_4), .ld(in_5), .clr(in_6));  // open: sel
endmodule

module EXT (
  input  [15:0] in_1,
  output [31:0] out_2,
  output [31:0] out_3
);

  assign out_2 = {{16{1'b0}}, in_1};  // Bit_Extender bit_extender_1
  assign out_3 = {{16{in_1[15]}}, in_1};  // Bit_Extender bit_extender_2
endmodule
