// Logisim project ppt ALU.circ as structural Verilog: 4 circuits, main circuit main
module main (
);

  wire [4:0] register_1_q;

  Register #(.width(5)) register_1 (.Q(register_1_q));  // open: D, en, clk, clr
  ROM #(.addrWidth(5), .dataWidth(32)) rom_1 ();  // open: addr, data, sel
  GRF grf_1 ();  // open: clk, reset, WE, WD, A1, A2, A3, RD1, RD2
  ALU alu_1 ();  // open: A, B, OP, Result, Zero
  RAM #(.addrWidth(5), .dataWidth(32), .bus("separate")) ram_1 ();  // open: addr, din, data, str, sel, clk, ld, clr
endmodule

module ALU (
  input  [31:0] A,
  input  [31:0] B,
  input  [3:0] OP,
  output [31:0] Result,
  output Zero
);

  wire comparator_1_eq, comparator_2_eq;
  wire [31:0] ADD, AND, OR, SUB;

  assign AND = A & B;  // AND_Gate and_1, 32 bits wide
  assign OR = A | B;  // OR_Gate or_1, 32 bits wide
  Adder #(.width(32)) adder_1 (.a(A), .b(B), .out(ADD));  // open: cin, cout
  Subtractor #(.width(32)) subtractor_1 (.a(A), .b(B), .out(SUB));  // open: bin, bout
  Comparator #(.width(4), .mode("unsigned")) comparator_1 (.a(OP), .b(4'b0111), .eq(comparator_1_eq));  // open: gt, lt
  Comparator #(.width(32), .mode("unsigned")) comparator_2 (
    .a(SUB), .b({32{1'b0}}), .eq(comparator_2_eq));  // open: gt, lt
  Multiplexer #(.select(4), .width(32), .disabled(0)) multiplexer_1 (
    .in0(AND), .in1(OR), .in2(ADD), .in6(SUB), .out(Result), .sel(OP));  // open: in3, in4, in5, in7, in8, in9, in10, in11, in12, in13, in14, in15, en
  and and_2 (Zero, comparator_1_eq, comparator_2_eq);
endmodule

module GRF (
  input  clk,
  input  reset,
  input  WE,
  input  [31:0] WD,
  input  [4:0] A1,
  input  [4:0] A2,
  input  [4:0] A3,
  output [31:0] RD1,
  output [31:0] RD2
);

  wire and_1_out, and_2_out, and_3_out, and_4_out, and_5_out, and_6_out, and_7_out, and_8_out, and_9_out,
       and_10_out, and_11_out, and_12_out, and_13_out, and_14_out, and_15_out, and_16_out, and_17_out,
       and_18_out, and_19_out, and_20_out, and_21_out, and_22_out, and_23_out, and_24_out, and_25_out,
       and_26_out, and_27_out, and_28_out, and_29_out, and_30_out, and_31_out, d0, d1, d2, d3, d4, d5, d6,
       d7, d8, d9, d10, d11, d12, d13, d14, d15, d16, d17, d18, d19, d20, d21, d22, d23, d24, d25, d26, d27,
       d28, d29, d30, d31;
  wire [31:0] i0, i1, i2, i3, i4, i5, i6, i7, i8, i9, i10, i11, i12, i13, i14, i15, i16, i17, i18, i19, i20,
       i21, i22, i23, i24, i25, i26, i27, i28, i29, i30, i31, o0, o1, o2, o3, o4, o5, o6, o7, o8, o9, o10,
       o11, o12, o13, o14, o15, o16, o17, o18, o19, o20, o21, o22, o23, o24, o25, o26, o27, o28, o29, o30,
       o31;

  Multiplexer #(.select(5), .width(32)) multiplexer_1 (
    .in0(o0), .in1(o1), .in2(o2), .in3(o3), .in4(o4), .in5(o5), .in6(o6), .in7(o7), .in8(o8), .in9(o9),
    .in10(o10), .in11(o11), .in12(o12), .in13(o13), .in14(o14), .in15(o15), .in16(o16), .in17(o17),
    .in18(o18), .in19(o19), .in20(o20), .in21(o21), .in22(o22), .in23(o23), .in24(o24), .in25(o25),
    .in26(o26), .in27(o27), .in28(o28), .in29(o29), .in30(o30), .in31(o31), .out(RD1), .sel(A1));  // open: en
  Register #(.width(32)) register_1 (.D(i0), .Q(o0), .clk(clk), .clr(reset));  // open: en
  Register #(.width(32)) register_2 (.D(i8), .Q(o8), .clk(clk), .clr(reset));  // open: en
  Register #(.width(32)) register_3 (.D(i16), .Q(o16), .clk(clk), .clr(reset));  // open: en
  Register #(.width(32)) register_4 (.D(i24), .Q(o24), .clk(clk), .clr(reset));  // open: en
  Register #(.width(32)) register_5 (.D(i1), .Q(o1), .clk(clk), .clr(reset));  // open: en
  Register #(.width(32)) register_6 (.D(i9), .Q(o9), .clk(clk), .clr(reset));  // open: en
  Register #(.width(32)) register_7 (.D(i17), .Q(o17), .clk(clk), .clr(reset));  // open: en
  Register #(.width(32)) register_8 (.D(i25), .Q(o25), .clk(clk), .clr(reset));  // open: en
  Multiplexer #(.select(5), .width(32)) multiplexer_2 (
    .in0(o0), .in1(o1), .in2(o2), .in3(o3), .in4(o4), .in5(o5), .in6(o6), .in7(o7), .in8(o8), .in9(o9),
    .in10(o10), .in11(o11), .in12(o12), .in13(o13), .in14(o14), .in15(o15), .in16(o16), .in17(o17),
    .in18(o18), .in19(o19), .in20(o20), .in21(o21), .in22(o22), .in23(o23), .in24(o24), .in25(o25),
    .in26(o26), .in27(o27), .in28(o28), .in29(o29), .in30(o30), .in31(o31), .out(RD2), .sel(A2));  // open: en
  Register #(.width(32)) register_9 (.D(i2), .Q(o2), .clk(clk), .clr(reset));  // open: en
  Register #(.width(32)) register_10 (.D(i10), .Q(o10), .clk(clk), .clr(reset));  // open: en
  Register #(.width(32)) register_11 (.D(i18), .Q(o18), .clk(clk), .clr(reset));  // open: en
  Register #(.width(32)) register_12 (.D(i26), .Q(o26), .clk(clk), .clr(reset));  // open: en
  Register #(.width(32)) register_13 (.D(i3), .Q(o3), .clk(clk), .clr(reset));  // open: en
  Register #(.width(32)) register_14 (.D(i11), .Q(o11), .clk(clk), .clr(reset));  // open: en
  Register #(.width(32)) register_15 (.D(i19), .Q(o19), .clk(clk), .clr(reset));  // open: en
  Register #(.width(32)) register_16 (.D(i27), .Q(o27), .clk(clk), .clr(reset));  // open: en
  Register #(.width(32)) register_17 (.D(i4), .Q(o4), .clk(clk), .clr(reset));  // open: en
  Register #(.width(32)) register_18 (.D(i12), .Q(o12), .clk(clk), .clr(reset));  // open: en
  Register #(.width(32)) register_19 (.D(i20), .Q(o20), .clk(clk), .clr(reset));  // open: en
  Register #(.width(32)) register_20 (.D(i28), .Q(o28), .clk(clk), .clr(reset));  // open: en
  Decoder #(.select(5)) decoder_1 (
    .out0(d0), .out1(d1), .out2(d2), .out3(d3), .out4(d4), .out5(d5), .out6(d6), .out7(d7), .out8(d8),
    .out9(d9), .out10(d10), .out11(d11), .out12(d12), .out13(d13), .out14(d14), .out15(d15), .out16(d16),
    .out17(d17), .out18(d18), .out19(d19), .out20(d20), .out21(d21), .out22(d22), .out23(d23), .out24(d24),
    .out25(d25), .out26(d26), .out27(d27), .out28(d28), .out29(d29), .out30(d30), .out31(d31), .sel(A3));  // open: en
  Register #(.width(32)) register_21 (.D(i5), .Q(o5), .clk(clk), .clr(reset));  // open: en
  Register #(.width(32)) register_22 (.D(i13), .Q(o13), .clk(clk), .clr(reset));  // open: en
  Register #(.width(32)) register_23 (.D(i21), .Q(o21), .clk(clk), .clr(reset));  // open: en
  Register #(.width(32)) register_24 (.D(i29), .Q(o29), .clk(clk), .clr(reset));  // open: en
  Register #(.width(32)) register_25 (.D(i6), .Q(o6), .clk(clk), .clr(reset));  // open: en
  Register #(.width(32)) register_26 (.D(i14), .Q(o14), .clk(clk), .clr(reset));  // open: en
  Register #(.width(32)) register_27 (.D(i22), .Q(o22), .clk(clk), .clr(reset));  // open: en
  Register #(.width(32)) register_28 (.D(i30), .Q(o30), .clk(clk), .clr(reset));  // open: en
  Multiplexer #(.width(32)) multiplexer_3 (.in0(o0), .in1(WD), .out(i0), .sel(1'b0));  // open: en
  Multiplexer #(.width(32)) multiplexer_4 (.in0(o4), .in1(WD), .out(i4), .sel(and_1_out));  // open: en
  and and_1 (and_1_out, d4, WE);
  Multiplexer #(.width(32)) multiplexer_5 (.in0(o8), .in1(WD), .out(i8), .sel(and_2_out));  // open: en
  and and_2 (and_2_out, d8, WE);
  Multiplexer #(.width(32)) multiplexer_6 (.in0(o12), .in1(WD), .out(i12), .sel(and_3_out));  // open: en
  buf and_3 (and_3_out, d12);  // AND_Gate
  Multiplexer #(.width(32)) multiplexer_7 (.in0(o16), .in1(WD), .out(i16), .sel(and_4_out));  // open: en
  and and_4 (and_4_out, d16, WE);
  Multiplexer #(.width(32)) multiplexer_8 (.in0(o20), .in1(WD), .out(i20), .sel(and_5_out));  // open: en
  buf and_5 (and_5_out, d20);  // AND_Gate
  Multiplexer #(.width(32)) multiplexer_9 (.in0(o24), .in1(WD), .out(i24), .sel(and_6_out));  // open: en
  and and_6 (and_6_out, d24, WE);
  Multiplexer #(.width(32)) multiplexer_10 (.in0(o28), .in1(WD), .out(i28), .sel(and_7_out));  // open: en
  buf and_7 (and_7_out, d28);  // AND_Gate
  Register #(.width(32)) register_29 (.D(i7), .Q(o7), .clk(clk), .clr(reset));  // open: en
  Register #(.width(32)) register_30 (.D(i15), .Q(o15), .clk(clk), .clr(reset));  // open: en
  Register #(.width(32)) register_31 (.D(i23), .Q(o23), .clk(clk), .clr(reset));  // open: en
  Register #(.width(32)) register_32 (.D(i31), .Q(o31), .clk(clk), .clr(reset));  // open: en
  Multiplexer #(.width(32)) multiplexer_11 (.in0(o1), .in1(WD), .out(i1), .sel(and_8_out));  // open: en
  and and_8 (and_8_out, d1, WE);
  Multiplexer #(.width(32)) multiplexer_12 (.in0(o5), .in1(WD), .out(i5), .sel(and_9_out));  // open: en
  and and_9 (and_9_out, d5, WE);
  Multiplexer #(.width(32)) multiplexer_13 (.in0(o9), .in1(WD), .out(i9), .sel(and_10_out));  // open: en
  and and_10 (and_10_out, d9, WE);
  Multiplexer #(.width(32)) multiplexer_14 (.in0(o13), .in1(WD), .out(i13), .sel(and_11_out));  // open: en
  buf and_11 (and_11_out, d13);  // AND_Gate
  Multiplexer #(.width(32)) multiplexer_15 (.in0(o17), .in1(WD), .out(i17), .sel(and_12_out));  // open: en
  and and_12 (and_12_out, d17, WE);
  Multiplexer #(.width(32)) multiplexer_16 (.in0(o21), .in1(WD), .out(i21), .sel(and_13_out));  // open: en
  buf and_13 (and_13_out, d21);  // AND_Gate
  Multiplexer #(.width(32)) multiplexer_17 (.in0(o25), .in1(WD), .out(i25), .sel(and_14_out));  // open: en
  and and_14 (and_14_out, d25, WE);
  Multiplexer #(.width(32)) multiplexer_18 (.in0(o29), .in1(WD), .out(i29), .sel(and_15_out));  // open: en
  buf and_15 (and_15_out, d29);  // AND_Gate
  Multiplexer #(.width(32)) multiplexer_19 (.in0(o2), .in1(WD), .out(i2), .sel(and_16_out));  // open: en
  and and_16 (and_16_out, d2, WE);
  Multiplexer #(.width(32)) multiplexer_20 (.in0(o6), .in1(WD), .out(i6), .sel(and_17_out));  // open: en
  and and_17 (and_17_out, d6, WE);
  Multiplexer #(.width(32)) multiplexer_21 (.in0(o10), .in1(WD), .out(i10), .sel(and_18_out));  // open: en
  and and_18 (and_18_out, d10, WE);
  Multiplexer #(.width(32)) multiplexer_22 (.in0(o14), .in1(WD), .out(i14), .sel(and_19_out));  // open: en
  buf and_19 (and_19_out, d14);  // AND_Gate
  Multiplexer #(.width(32)) multiplexer_23 (.in0(o18), .in1(WD), .out(i18), .sel(and_20_out));  // open: en
  and and_20 (and_20_out, d18, WE);
  Multiplexer #(.width(32)) multiplexer_24 (.in0(o22), .in1(WD), .out(i22), .sel(and_21_out));  // open: en
  buf and_21 (and_21_out, d22);  // AND_Gate
  Multiplexer #(.width(32)) multiplexer_25 (.in0(o26), .in1(WD), .out(i26), .sel(and_22_out));  // open: en
  and and_22 (and_22_out, d26, WE);
  Multiplexer #(.width(32)) multiplexer_26 (.in0(o30), .in1(WD), .out(i30), .sel(and_23_out));  // open: en
  buf and_23 (and_23_out, d30);  // AND_Gate
  Multiplexer #(.width(32)) multiplexer_27 (.in0(o3), .in1(WD), .out(i3), .sel(and_24_out));  // open: en
  and and_24 (and_24_out, d3, WE);
  Multiplexer #(.width(32)) multiplexer_28 (.in0(o7), .in1(WD), .out(i7), .sel(and_25_out));  // open: en
  and and_25 (and_25_out, d7, WE);
  Multiplexer #(.width(32)) multiplexer_29 (.in0(o11), .in1(WD), .out(i11), .sel(and_26_out));  // open: en
  and and_26 (and_26_out, d11, WE);
  Multiplexer #(.width(32)) multiplexer_30 (.in0(o15), .in1(WD), .out(i15), .sel(and_27_out));  // open: en
  buf and_27 (and_27_out, d15);  // AND_Gate
  Multiplexer #(.width(32)) multiplexer_31 (.in0(o19), .in1(WD), .out(i19), .sel(and_28_out));  // open: en
  and and_28 (and_28_out, d19, WE);
  Multiplexer #(.width(32)) multiplexer_32 (.in0(o23), .in1(WD), .out(i23), .sel(and_29_out));  // open: en
  buf and_29 (and_29_out, d23);  // AND_Gate
  Multiplexer #(.width(32)) multiplexer_33 (.in0(o27), .in1(WD), .out(i27), .sel(and_30_out));  // open: en
  and and_30 (and_30_out, d27, WE);
  Multiplexer #(.width(32)) multiplexer_34 (.in0(o31), .in1(WD), .out(i31), .sel(and_31_out));  // open: en
  buf and_31 (and_31_out, d31);  // AND_Gate

  // Other names for the same wires on the sheet: c = clk; rs = reset
endmodule

module Splitter (
  input  [31:0] in_1
);
endmodule
