// Logisim project fib1.circ as structural Verilog: 1 circuit, main circuit main
module main (
  input  [2:0] N,
  output [3:0] Nth
);

  wire and_1_out, clock_1_out, comparator_1_gt, comparator_1_lt, comparator_2_eq, counter_1_carry, not_1_out,
       not_2_out;
  wire [3:0] adder_1_out, bit_extender_1_out, counter_1_q, out1, out2, register_1_q, register_2_q;

  and and_1 (and_1_out, not_1_out, clock_1_out);
  not not_1 (not_1_out, counter_1_carry);
  Counter #(.width(4), .max('hf)) counter_1 (
    .Q(counter_1_q), .carry(counter_1_carry), .clk(and_1_out));  // open: load, D, count, clr
  assign bit_extender_1_out = {{1{1'b0}}, N};  // Bit_Extender bit_extender_1
  Register #(.width(4)) register_1 (.D(out1), .Q(register_1_q), .clk(clock_1_out));  // open: en, clr
  Clock clock_1 (.out(clock_1_out));
  Comparator #(.width(4), .mode("unsigned")) comparator_1 (
    .a(counter_1_q), .b(bit_extender_1_out), .gt(comparator_1_gt), .lt(comparator_1_lt));  // open: eq
  Comparator #(.width(4), .mode("unsigned")) comparator_2 (
    .a(counter_1_q), .b(4'b0001), .eq(comparator_2_eq));  // open: gt, lt
  Register #(.width(4)) register_2 (.D(out2), .Q(register_2_q), .clk(clock_1_out));  // open: en, clr
  Adder #(.width(4)) adder_1 (
    .a(register_1_q), .b(register_2_q), .out(adder_1_out), .cin(comparator_2_eq));  // open: cout
  Multiplexer #(.width(4)) multiplexer_1 (
    .in0(adder_1_out), .in1(register_1_q), .out(out1), .sel(comparator_1_gt));  // open: en
  Multiplexer #(.width(4)) multiplexer_2 (
    .in0(register_1_q), .in1(register_2_q), .out(out2), .sel(comparator_1_gt));  // open: en
  not not_2 (not_2_out, comparator_1_lt);
  Multiplexer #(.width(4)) multiplexer_3 (.in0(4'b0000), .in1(out1), .out(Nth), .sel(not_2_out));  // open: en
endmodule
