// Logisim project fib2.circ as structural Verilog: 2 circuits, main circuit main
module main (
  input  [31:0] N,
  output [31:0] Nth
);

  wire clock, \end , first, is1, not_1_out, not_2_out, run;
  wire [4:0] bit_extender_1_out;
  wire [5:0] cnt, subtractor_1_out;
  wire [31:0] A, a1, a2, a_t, B, b1, b2, C, c1, c2, D, d1, d2, d_t, E, e1, F, f1, f_t, G, g1, g_t, H, h1,
       h_t, shifter_1_out;

  Clock clock_1 (.out(clock));
  Register #(.width(32)) register_1 (.D(A), .Q(a_t), .clk(clock));  // open: en, clr
  Register #(.width(32)) register_2 (.D(B), .Q(b1), .clk(clock));  // open: en, clr
  Register #(.width(32)) register_3 (.D(E), .Q(e1), .clk(clock));  // open: en, clr
  Register #(.width(32)) register_4 (.D(F), .Q(f_t), .clk(clock));  // open: en, clr
  Adder #(.width(32)) adder_1 (.a(a_t), .b({32{1'b0}}), .out(a1), .cin(first));  // open: cout
  Adder #(.width(32)) adder_2 (.a(d_t), .b({32{1'b0}}), .out(d1), .cin(first));  // open: cout
  mul mul_1 (.a(a1), .b(b1), .c(c1), .d(d1), .e(e1), .f(f1), .g(g1), .h(h1), .A_2(a2), .B_2(b2), .C_2(c2), .D_2(d2));
  Register #(.width(32)) register_5 (.D(C), .Q(c1), .clk(clock));  // open: en, clr
  Register #(.width(32)) register_6 (.D(G), .Q(g_t), .clk(clock));  // open: en, clr
  Multiplexer #(.width(32)) multiplexer_1 (.in0(a1), .in1(a2), .out(A), .sel(is1));  // open: en
  Multiplexer #(.width(32)) multiplexer_2 (.in0(b1), .in1(b2), .out(B), .sel(is1));  // open: en
  Multiplexer #(.width(32)) multiplexer_3 (.in0(c1), .in1(c2), .out(C), .sel(is1));  // open: en
  Multiplexer #(.width(32)) multiplexer_4 (.in0(d1), .in1(d2), .out(D), .sel(is1));  // open: en
  Bit_Extender #(.in_width(6), .out_width(5)) bit_extender_1 (.in(subtractor_1_out), .out(bit_extender_1_out));
  Subtractor #(.width(6)) subtractor_1 (.a(cnt), .b(6'b000001), .out(subtractor_1_out));  // open: bin, bout
  and and_1 (run, clock, not_1_out);
  not not_1 (not_1_out, \end );
  Register #(.width(32)) register_7 (.D(D), .Q(d_t), .clk(clock));  // open: en, clr
  Register #(.width(32)) register_8 (.D(H), .Q(h_t), .clk(clock));  // open: en, clr
  Shifter #(.width(32), .shift("lr")) shifter_1 (.in(N), .\dist (bit_extender_1_out), .out(shifter_1_out));
  not not_2 (not_2_out, \end );
  mul mul_2 (.a(e1), .b(f1), .c(g1), .d(h1), .e(e1), .f(f1), .g(g1), .h(h1), .A_2(E), .B_2(F), .C_2(G), .D_2(H));
  and and_2 (is1, shifter_1_out[0], not_2_out);
  Counter #(.width(6), .max('h21)) counter_1 (.Q(cnt), .carry(\end ), .clk(run));  // open: load, D, count, clr
  Adder #(.width(32)) adder_3 (.a(f_t), .b({32{1'b0}}), .out(f1), .cin(first));  // open: cout
  Adder #(.width(32)) adder_4 (.a(g_t), .b({32{1'b0}}), .out(g1), .cin(first));  // open: cout
  Adder #(.width(32)) adder_5 (.a(h_t), .b({32{1'b0}}), .out(h1), .cin(first));  // open: cout
  Multiplexer #(.width(32)) multiplexer_5 (.in0({32{1'b0}}), .in1(C), .out(Nth), .sel(\end ));  // open: en
  Comparator #(.width(6), .mode("unsigned")) comparator_1 (.a(cnt), .b(6'b000001), .eq(first));  // open: gt, lt

  // Other names for the same wires on the sheet: b_t[31:0] = b1; c_t[31:0] = c1; e_t[31:0] = e1; in[31:0] = N
endmodule

module mul (
  input  [31:0] a,
  input  [31:0] b,
  input  [31:0] c,
  input  [31:0] d,
  input  [31:0] e,
  input  [31:0] f,
  input  [31:0] g,
  input  [31:0] h,
  output [31:0] A_2,
  output [31:0] B_2,
  output [31:0] C_2,
  output [31:0] D_2
);

  wire [31:0] multiplier_1_out, multiplier_2_out, multiplier_3_out, multiplier_4_out, multiplier_5_out,
       multiplier_6_out, multiplier_7_out, multiplier_8_out;

  Multiplier #(.width(32)) multiplier_1 (.a(a), .b(e), .out(multiplier_1_out));  // open: cin, cout
  Multiplier #(.width(32)) multiplier_2 (.a(b), .b(g), .out(multiplier_2_out));  // open: cin, cout
  Multiplier #(.width(32)) multiplier_3 (.a(a), .b(f), .out(multiplier_3_out));  // open: cin, cout
  Multiplier #(.width(32)) multiplier_4 (.a(b), .b(h), .out(multiplier_4_out));  // open: cin, cout
  Multiplier #(.width(32)) multiplier_5 (.a(c), .b(e), .out(multiplier_5_out));  // open: cin, cout
  Multiplier #(.width(32)) multiplier_6 (.a(d), .b(g), .out(multiplier_6_out));  // open: cin, cout
  Multiplier #(.width(32)) multiplier_7 (.a(c), .b(f), .out(multiplier_7_out));  // open: cin, cout
  Multiplier #(.width(32)) multiplier_8 (.a(d), .b(h), .out(multiplier_8_out));  // open: cin, cout
  Adder #(.width(32)) adder_1 (.a(multiplier_1_out), .b(multiplier_2_out), .out(A_2));  // open: cin, cout
  Adder #(.width(32)) adder_2 (.a(multiplier_3_out), .b(multiplier_4_out), .out(B_2));  // open: cin, cout
  Adder #(.width(32)) adder_3 (.a(multiplier_5_out), .b(multiplier_6_out), .out(C_2));  // open: cin, cout
  Adder #(.width(32)) adder_4 (.a(multiplier_7_out), .b(multiplier_8_out), .out(D_2));  // open: cin, cout
endmodule
