// Logisim project mod5.circ as structural Verilog: 3 circuits, main circuit mod5
module mod5 (
  input  In,
  output S0,
  output S1,
  output S2,
  output S3,
  output S4
);

  wire clock_1_out;
  wire [1:0] register_1_q, tran_1_out_3;

  Register #(.width(2)) register_1 (.D(tran_1_out_3), .Q(register_1_q), .clk(clock_1_out));  // open: en, clr
  Clock clock_1 (.out(clock_1_out));
  Decoder #(.select(2)) decoder_1 (.out0(S1), .out1(S2), .out2(S3), .out3(S4), .sel(tran_1_out_3));  // open: en
  tran_2 tran_1 (.in_1(register_1_q), .in_2(In), .out_3(tran_1_out_3));

  assign S0 = 1'b0;
endmodule

module \tran  (
  input  a,
  input  b,
  input  c,
  output a2,
  output b2
);

  wire nand_1_out, nand_2_out, nand_3_out, nand_4_out, nand_5_out, nand_6_out, nand_7_out, nand_8_out,
       nand_9_out, nand_10_out, nand_11_out, nand_12_out, nand_13_out, nand_14_out;

  nand nand_1 (nand_1_out, a, a);
  nand nand_2 (nand_2_out, b, b);
  nand nand_3 (nand_3_out, a, a);
  nand nand_4 (nand_4_out, b, b);
  nand nand_5 (nand_5_out, a, a);
  nand nand_6 (nand_6_out, c, c);
  nand nand_7 (nand_7_out, b, b);
  nand nand_8 (nand_8_out, c, c);
  nand nand_9 (nand_9_out, nand_1_out, b);
  nand nand_10 (nand_10_out, a, nand_2_out);
  nand nand_11 (nand_11_out, nand_3_out, nand_4_out, c);
  nand nand_12 (nand_12_out, nand_5_out, b, nand_6_out);
  nand nand_13 (nand_13_out, a, nand_7_out, nand_8_out);
  nand nand_14 (nand_14_out, a, b, c);
  nand nand_15 (a2, nand_9_out, nand_10_out);
  nand nand_16 (b2, nand_11_out, nand_12_out, nand_13_out, nand_14_out);
endmodule

module tran_2 (
  input  [1:0] in_1,
  input  in_2,
  output [1:0] out_3
);

  \tran  tran_1 (.a(in_1[1]), .b(in_1[0]), .c(in_2), .a2(out_3[1]), .b2(out_3[0]));
endmodule
