// Logisim project sort.circ as structural Verilog: 4 circuits, main circuit 4bit_sort
module _4bit_sort (
  input  [3:0] A,
  input  [3:0] B,
  input  [3:0] C,
  input  [3:0] D,
  output [3:0] _1,
  output [3:0] _2,
  output [3:0] _3,
  output [3:0] _4
);

  wire [3:0] cmp_1_o1, cmp_1_o2, cmp_2_o1, cmp_2_o2, cmp_3_o1, cmp_4_o1, cmp_4_o2, cmp_5_o1;

  cmp cmp_1 (.I1(A), .I2(B), .O1(cmp_1_o1), .O2(cmp_1_o2));
  cmp cmp_2 (.I1(cmp_1_o2), .I2(C), .O1(cmp_2_o1), .O2(cmp_2_o2));
  cmp cmp_3 (.I1(cmp_2_o2), .I2(D), .O1(cmp_3_o1), .O2(_4));
  cmp cmp_4 (.I1(cmp_1_o1), .I2(cmp_2_o1), .O1(cmp_4_o1), .O2(cmp_4_o2));
  cmp cmp_5 (.I1(cmp_4_o2), .I2(cmp_3_o1), .O1(cmp_5_o1), .O2(_3));
  cmp cmp_6 (.I1(cmp_4_o1), .I2(cmp_5_o1), .O1(_1), .O2(_2));
endmodule

module _1bit_swap (
  input  I1,
  input  I2,
  input  S,
  output O1,
  output O2
);

  wire and_1_out, and_2_out, and_3_out, and_4_out, not_1_out;

  not not_1 (not_1_out, S);
  and and_1 (and_1_out, I1, not_1_out);
  and and_2 (and_2_out, S, I2);
  and and_3 (and_3_out, I2, not_1_out);
  and and_4 (and_4_out, S, I1);
  or or_1 (O1, and_1_out, and_2_out);
  or or_2 (O2, and_3_out, and_4_out);
endmodule

module _4bit_swap (
  input  [3:0] I1,
  input  [3:0] I2,
  input  S,
  output [3:0] O1,
  output [3:0] O2
);

  _1bit_swap u_1bit_swap_1 (.I1(I1[0]), .I2(I2[0]), .S(S), .O1(O1[0]), .O2(O2[0]));
  _1bit_swap u_1bit_swap_2 (.I1(I1[1]), .I2(I2[1]), .S(S), .O1(O1[1]), .O2(O2[1]));
  _1bit_swap u_1bit_swap_3 (.I1(I1[2]), .I2(I2[2]), .S(S), .O1(O1[2]), .O2(O2[2]));
  _1bit_swap u_1bit_swap_4 (.I1(I1[3]), .I2(I2[3]), .S(S), .O1(O1[3]), .O2(O2[3]));
endmodule

module cmp (
  input  [3:0] I1,
  input  [3:0] I2,
  output [3:0] O1,
  output [3:0] O2
);

  wire comparator_1_gt;

  Comparator #(.width(4), .mode("unsigned")) comparator_1 (.a(I1), .b(I2), .gt(comparator_1_gt));  // open: eq, lt
  _4bit_swap u_4bit_swap_1 (.I1(I1), .I2(I2), .S(comparator_1_gt), .O1(O1), .O2(O2));
endmodule
